# Fritzing sketch I2C_Arduino_RPi (saved by Fritzing 0.9.3b)
breadboards: 1

parts:
  Part1 = Arduino Uno (Rev3)
  Part2 = Arduino Micro (Rev3)  # not connected
  Part3 = Adafruit T-Cobbler Plus [part_number="Adafruit #1989 and #2028"]
  LLC1 = Logic Level Converter [package="Breakout board"]
  OLED1 = 128x32 I2C Monochrome OLED Display

nets:
  N1: Part1.A4/SDA, LLC1.LV1, OLED1.SDA
  N2: Part1.A5/SCL, LLC1.LV2, OLED1.SCL
  5V: Part1.5V, LLC1.LV, OLED1.3.3V
  GND: Part1.GND, Part3.GND, LLC1.L-GND, LLC1.H-GND, OLED1.GND
  N3: Part3.SDA, LLC1.HV1
  N4: Part3.SCL, LLC1.HV2
  N5: Part3.+3.3V_2, LLC1.HV

notes:
  5 V power bus
  5 volt i2c bus
  To Raspberry Pi GPIO
  Note: OLED on diagram shows 3.3V. Actual part and power connection 5V.
  5V side of Level Controller
  3.3V side of Level Controller

custom parts:
  Adafruit T-Cobbler Plus: The Raspberry Pi has landed on the Maker World like a 40-GPIO pinned, quad-USB ported, credit card sized bomb of DIY joy. And while you can use most of our great Model B accessories by hooking up our downgrade cable, its probably a good time to upgrade your set up and accessorize using all of the 40 pins. That's why we now carry the Assembled Adafruit Pi T-Cobbler Plus - Breakout + Cable for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
  Logic Level Converter: 5V to/from 3.3V logic level converter
